# Fritzing sketch Home_Monitor_System (saved by Fritzing 0.9.3b)
circuit board: 6.19641cm x 5.14299cm
breadboards: 1

parts:
  Blue = LED - 5mm [color="Blue (505nm)" package="5 mm [THT]"]
  B1 = Resistor [tolerance=±5% resistance=330 package=THT]
  MQ-3 = female pin header, 4 pins [form="♀ (female)"]
  Buzzer = female pin header, 3 pins [form="♀ (female)"]
  HC-SR501 = female pin header, 3 pins [form="♀ (female)"]
  SHT31-D = female pin header, 7 pins [form="♀ (female)"]
  ADC1 = MCP3008 [package=dil16]
  Raspberry_Pi_1 = Raspberry Pi 3 [part_number=RPI-3-V1.2]

nets:
  N1: Blue.cathode, MQ-3.pin3, Buzzer.pin1, HC-SR501.pin3, SHT31-D.pin6, ADC1.DGND, ADC1.AGND, Raspberry_Pi_1.GND
  N2: Blue.anode, B1.Pin_0
  N3: B1.Pin_1, Raspberry_Pi_1.GIPO22
  N4: MQ-3.pin1, ADC1.CH0
  VDD: MQ-3.pin4, HC-SR501.pin1, ADC1.VREF, ADC1.VDD, Raspberry_Pi_1.5V
  N5: Buzzer.pin2, SHT31-D.pin7, Raspberry_Pi_1.3v3
  N6: Buzzer.pin3, Raspberry_Pi_1.GIPO5
  N7: HC-SR501.pin2, Raspberry_Pi_1.GIPO26
  N8: SHT31-D.pin4, Raspberry_Pi_1.GPIO2
  N9: SHT31-D.pin5, Raspberry_Pi_1.GPIO3
  N10: ADC1.CS/SHDN, Raspberry_Pi_1.GIPO8
  N11: ADC1.Din, Raspberry_Pi_1.GIPO10
  N12: ADC1.Dout, Raspberry_Pi_1.GIPO9
  N13: ADC1.CLK, Raspberry_Pi_1.GIPO11

notes:
  SDA
  SCL
  GND
  VCC
  IN
  OUT
  N/A
  BUZZER
  MQ-2
  SHT31-D
  HC-SR501
  Smart Home Monitor System
  320Ω
  ADCL
  D
  LED
